# Fritzing sketch water_bottle_pump_circuit (saved by Fritzing 0.9.3b)
breadboards: 1

parts:
  Digispark1 = Digispark
  U1 = LIPO-1000mAh [package=lipo-1000]
  Charger = USB LiPoly Charger
  Part3 = Adafruit VL53L0X Time of Flight Distance Sensor [part_number="Adafruit #3317"]
  Air_Pump = DC Motor
  7886 = 555 Timer [package="SO8 [SMD]"]  # not connected
  D1 = Diode [package=diode-hv]
  D2 = Diode [package=diode-hv]
  Solenoid = Solenoid

nets:
  VCC: Digispark1.VCC, U1.+, Charger.VBAT, Part3.VIN
  GND: Digispark1.GND, U1.-, Charger.GND, Part3.GND
  N1: Digispark1.P0, Part3.SDA
  N2: Digispark1.P2, Part3.SCL
  N3: Air_Pump.pin_1, D1.C
  N4: Air_Pump.pin_2, D2.A
  N5: D1.A, Solenoid.pin1
  N6: D2.C, Solenoid.pin2

custom parts:
  Digispark: The Digispark is an Attiny85 based microcontroller development board similar to the Arduino line, only cheaper, smaller, and a bit less powerful. With a whole host of shields to extend its functionality and the ability to use the familiar Arduino IDE the Digispark is a great way to jump into electronics, or perfect for when an Arduino is too big or too much.
  Adafruit VL53L0X Time of Flight Distance Sensor: The VL53L0X is a Time of Flight distance sensor like no other you've used! The sensor contains a very tiny invisible laser source, and a matching sensor. The VL53L0X can detect the "time of flight", or how long the light has taken to bounce back to the sensor. Since it uses a very narrow light source, it is good for determining distance of only the surface directly in front of it. Unlike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
